// Logisim project alu.circ as structural Verilog: 1 circuit, main circuit alu
module alu (
  input  [31:0] A,
  input  [31:0] B,
  input  [3:0] ALUSel,
  output [31:0] Result
);

  wire xor_2_out;
  wire [0:0] adder_4_cout, slt0;
  wire [31:0] add0, adder_1_out, adder_2_out, adder_4_out, adder_5_out, and0, divu0, mul0, mulh0, mulhu0,
       multiplexer_1_out, multiplexer_2_out, multiplexer_4_out, multiplier_3_cout, multiplier_3_out,
       not_1_out, not_2_out, not_3_out, not_4_out, or0, remu0, sll0, sra0, srl0, sub0, xor0;

  assign not_1_out = ~A;  // NOT_Gate not_1, 32 bits wide
  assign not_2_out = ~B;  // NOT_Gate not_2, 32 bits wide
  Adder #(.width(32)) adder_1 (.a(not_1_out), .b(32'h1), .out(adder_1_out));  // open: cin, cout
  Adder #(.width(32)) adder_2 (.a(not_2_out), .b(32'h1), .out(adder_2_out));  // open: cin, cout
  Multiplexer #(.width(32), .enable("false")) multiplexer_1 (
    .in0(B), .in1(adder_2_out), .out(multiplexer_1_out), .sel(B[31]));
  Adder #(.width(32)) adder_3 (.a(A), .b(B), .out(add0));  // open: cin, cout
  assign and0 = A & B;  // AND_Gate and_1, 32 bits wide
  assign or0 = A | B;  // OR_Gate or_1, 32 bits wide
  assign xor0 = A ^ B;  // XOR_Gate xor_1, 32 bits wide
  Shifter #(.width(32), .shift("lr")) shifter_1 (.in(A), .\dist (B[4:0]), .out(srl0));
  Shifter #(.width(32), .shift("ar")) shifter_2 (.in(A), .\dist (B[4:0]), .out(sra0));
  Shifter #(.width(32)) shifter_3 (.in(A), .\dist (B[4:0]), .out(sll0));
  Comparator #(.width(32)) comparator_1 (.a(A), .b(B), .lt(slt0[0]));  // open: gt, eq
  Divider #(.width(32)) divider_1 (.a(A), .b(B), .out(divu0));  // open: upper, rem
  Divider #(.width(32)) divider_2 (.a(A), .b(B), .rem(remu0));  // open: out, upper
  Multiplier #(.width(32)) multiplier_1 (.a(A), .b(B), .out(mul0));  // open: cin, cout
  Multiplier #(.width(32)) multiplier_2 (.a(A), .b(B), .cout(mulhu0));  // open: out, cin
  Subtractor #(.width(32)) subtractor_1 (.a(A), .b(B), .out(sub0));  // open: bin, bout
  Multiplexer #(.width(32), .enable("false")) multiplexer_2 (
    .in0(A), .in1(adder_1_out), .out(multiplexer_2_out), .sel(A[31]));
  Multiplier #(.width(32)) multiplier_3 (
    .a(multiplexer_2_out), .b(multiplexer_1_out), .out(multiplier_3_out), .cout(multiplier_3_cout));  // open: cin
  assign not_3_out = ~multiplier_3_out;  // NOT_Gate not_3, 32 bits wide
  assign not_4_out = ~multiplier_3_cout;  // NOT_Gate not_4, 32 bits wide
  Adder #(.width(32)) adder_4 (.a(not_3_out), .b(32'h1), .out(adder_4_out), .cout(adder_4_cout[0]));  // open: cin
  Adder #(.width(32)) adder_5 (.a({{31{1'b0}}, adder_4_cout[0]}), .b(not_4_out), .out(adder_5_out));  // open: cin, cout
  Multiplexer #(.select(4), .width(32), .enable("false")) multiplexer_3 (
    .in0(add0), .in1(and0), .in2(or0), .in3(xor0), .in4(srl0), .in5(sra0), .in6(sll0),
    .in7({{31{1'b0}}, slt0[0]}), .in8(divu0), .in9(remu0), .in10(mul0), .in11(mulhu0), .in12(sub0), .in13(B),
    .in14(mulh0), .out(Result), .sel(ALUSel));  // open: in15
  Multiplexer #(.width(32), .enable("false")) multiplexer_4 (
    .in0(multiplier_3_out), .in1(adder_4_out), .out(multiplexer_4_out), .sel(xor_2_out));
  Multiplexer #(.width(32), .enable("false")) multiplexer_5 (
    .in0(multiplier_3_cout), .in1(adder_5_out), .out(mulh0), .sel(xor_2_out));
  xor xor_2 (xor_2_out, A[31], B[31]);

  // Other names for the same wires on the sheet: Sel0 = A[31]; Sel1 = B[31]; sltTemp = slt0[0]

  // Notes on the sheet:
  //   INPUTS to your circuit
  //   and
  //   xor
  //   add
  //   or
  //   srl
  //   sra
  //   sll
  //   slt
  //   divu
  //   remu
  //   mul
  //   mulhu
  //   sub
  //   DON'T CHANGE THE LOCATIONS OF THE INPUTS AND OUTPUTS!
  //   bsel
  //   OUTPUT from your circuit
endmodule
