// Logisim project cpu.circ as structural Verilog: 4 circuits, main circuit main
module main (
  input  [31:0] INSTRUCTION,
  input  CLOCK,
  output [31:0] PROGRAM_COUNTER,
  output [31:0] ra,
  output [31:0] sp,
  output [31:0] t0,
  output [31:0] t1,
  output [31:0] t2,
  output [31:0] s0,
  output [31:0] s1,
  output [31:0] a0
);

  wire ASel, BrEq, BrLt, BrUn, BSel, comparator_1_eq, DMEM_p1, DMEM_p5, MemRW, not_1_out, PCSel, RegWEn;
  wire [1:0] WBSel;
  wire [2:0] ImmSel;
  wire [3:0] ALUSel;
  wire [6:0] INSTRUCTION_OUT;
  wire [24:0] imm;
  wire [31:0] adder_2_out, ALU_Out, DMEM_Out, imm_Extended, multiplexer_1_out, multiplexer_3_out,
       multiplexer_4_out, PC4, PCPipe_q, register_1_q, rs1_Out, rs2_Out, wb;

  Multiplexer #(.width(32), .enable("false")) multiplexer_1 (
    .in0(PC4), .in1(ALU_Out), .out(multiplexer_1_out), .sel(PCSel));
  Register #(.width(32)) PC (.D(multiplexer_1_out), .clk(CLOCK), .Q(PROGRAM_COUNTER));  // open: en, clr
  Register #(.width(32)) register_1 (.D(INSTRUCTION), .clk(CLOCK), .Q(register_1_q));  // open: en, clr
  Adder #(.width(32)) adder_1 (.a(PROGRAM_COUNTER), .b(32'h4), .out(PC4));  // open: cin, cout
  Multiplexer #(.width(32), .enable("false")) multiplexer_2 (
    .in0(register_1_q), .in1(32'h13), .out({imm, INSTRUCTION_OUT}), .sel(not_1_out));
  Register #(.width(32)) PCPipe (.D(PROGRAM_COUNTER), .clk(CLOCK), .Q(PCPipe_q));  // open: en, clr
  Adder #(.width(32)) adder_2 (.a(PCPipe_q), .b(32'h4), .out(adder_2_out));  // open: cin, cout
  Comparator #(.width(32)) comparator_1 (.a(adder_2_out), .b(PROGRAM_COUNTER), .eq(comparator_1_eq));  // open: gt, lt
  not not_1 (not_1_out, comparator_1_eq);
  immGen immgen_1 (.inst_In(imm), .imm_Out(imm_Extended), .immSel(ImmSel));
  regfile_main RegFile (
    .rs2(imm[17:13]), .rd(imm[4:0]), .Read_Data_1(rs1_Out), .Read_Data_2(rs2_Out), .ra(ra), .sp(sp), .t0(t0),
    .t1(t1), .t2(t2), .s0(s0), .s1(s1), .a0(a0), .rs1(imm[12:8]), .Write_Data(wb), .RegWEn(RegWEn),
    .clk(CLOCK));
  branchComp branchcomp_1 (.rs1(rs1_Out), .rs2(rs2_Out), .BrUn(BrUn), .BrLt(BrLt), .BrEq(BrEq));
  Multiplexer #(.width(32), .enable("false")) multiplexer_3 (
    .in0(rs1_Out), .in1(PROGRAM_COUNTER), .out(multiplexer_3_out), .sel(ASel));
  Multiplexer #(.width(32), .enable("false")) multiplexer_4 (
    .in0(rs2_Out), .in1(imm_Extended), .out(multiplexer_4_out), .sel(BSel));
  alu Arithmetic_Logic_Unit (.Result(ALU_Out), .ALUSel(ALUSel), .A(multiplexer_3_out), .B(multiplexer_4_out));
  control control_1 (
    .inst_in({imm, INSTRUCTION_OUT}), .BrLt(BrLt), .BrEq(BrEq), .PCSel(PCSel), .RegWEn(RegWEn),
    .ImmSel(ImmSel), .BrUn(BrUn), .ASel(ASel), .BSel(BSel), .ALUSel(ALUSel), .MemRW(MemRW), .WBSel(WBSel));  // open: out_13
  // mem_main DMEM: pin names not known; wires that end beside it: DMEM_p1, DMEM_p1, ALU_Out, rs2_Out, DMEM_p5, CLOCK, MemRW, DMEM_Out
  Multiplexer #(.select(2), .width(32), .enable("false")) multiplexer_5 (
    .in0(PC4), .in1(ALU_Out), .in2(DMEM_Out), .out(wb), .sel(WBSel));  // open: in3

  // Other names for the same wires on the sheet: clk = CLOCK; INSTRUCTION_OUT[31:7] = imm; rd[4:0] = imm[4:0];
  //   rs1_In[4:0] = imm[12:8]; rs2_In[4:0] = imm[17:13]

  // Notes on the sheet:
  //   Output
  //   IMEM (do **NOT** move this)
  //   Inputs
  //   Inputs/Outputs for testing. Do **NOT** move these.
endmodule

module immGen (
  input  [24:0] inst_In,
  input  [2:0] immSel,
  output [31:0] imm_Out
);

  wire [31:0] I, S, SB, UJ;

  assign I = {{20{inst_In[24]}}, inst_In[24:13]};  // Bit_Extender bit_extender_1
  assign S = {{20{inst_In[24]}}, {inst_In[24:18], inst_In[4:0]}};  // Bit_Extender bit_extender_2
  assign SB = {{19{inst_In[24]}}, {inst_In[24], inst_In[0], inst_In[23:18], inst_In[4:1], 1'b0}};  // Bit_Extender bit_extender_3
  assign UJ = {{11{inst_In[24]}}, {inst_In[24], inst_In[12:5], inst_In[13], inst_In[23:14], 1'b0}};  // Bit_Extender bit_extender_4
  Multiplexer #(.select(3), .width(32), .enable("false")) multiplexer_1 (
    .in0(I), .in1(S), .in2(SB), .in3({inst_In[24:5], {12{1'b0}}}), .in4(UJ), .out(imm_Out), .sel(immSel));  // open: in5, in6, in7

  // Other names for the same wires on the sheet: Instruction_In[24:0] = inst_In; U[31:12] = inst_In[24:5]
endmodule

module control (
  input  [31:0] inst_in,
  input  BrLt,
  input  BrEq,
  output PCSel,
  output RegWEn,
  output [2:0] ImmSel,
  output BrUn,
  output ASel,
  output BSel,
  output [3:0] ALUSel,
  output MemRW,
  output [1:0] WBSel,
  output [19:0] out_13
);

  wire comparator_1_eq, comparator_2_eq, comparator_3_eq, or_1_out;
  wire [2:0] func3_d;

  or or_1 (or_1_out, comparator_1_eq, comparator_2_eq, comparator_3_eq);
  Comparator #(.width(5), .mode("unsigned")) comparator_1 (
    .a(inst_in[6:2]), .b(5'b01101), .eq(comparator_1_eq));  // open: gt, lt
  Comparator #(.width(5), .mode("unsigned")) comparator_2 (
    .a(inst_in[6:2]), .b(5'b11011), .eq(comparator_2_eq));  // open: gt, lt
  Comparator #(.width(5), .mode("unsigned")) comparator_3 (
    .a(inst_in[6:2]), .b(5'b11001), .eq(comparator_3_eq));  // open: gt, lt
  Multiplexer #(.width(3), .enable("false")) multiplexer_1 (
    .in0(inst_in[14:12]), .in1(3'b000), .out(func3_d), .sel(or_1_out));
  ROM #(.addrWidth(12), .dataWidth(20)) rom_1 (
    .addr({inst_in[6:2], func3_d, inst_in[30], inst_in[25], BrEq, BrLt}),
    .data({out_13[19:15], ImmSel, out_13[11], BrUn, ASel, BSel, ALUSel, out_13[3], MemRW, out_13[1:0]}));

  assign {out_13[14:12], out_13[10:4], out_13[2]} = {ImmSel, BrUn, ASel, BSel, ALUSel, MemRW};
  assign PCSel = out_13[17];
  assign RegWEn = out_13[16];
  assign WBSel = out_13[1:0];

  // Other names for the same wires on the sheet: func7_0 = inst_in[25]; func7_1 = inst_in[30];
  //   opcode[4:0] = inst_in[6:2];
  //   controlword[19:0] = {out_13[19:15], ImmSel, out_13[11], BrUn, ASel, BSel, ALUSel, out_13[3], MemRW, out_13[1:0]};
  //   func3[2:0] = inst_in[14:12]

  // Notes on the sheet:
  //   contents of rom_1 (hex, n*v repeats v):
  //   48*10102 464*0 16*10101 4*10161 12*0 16*10171 16*0 16*10131 4*10141 4*0 4*10151 4*0 16*10121
  //   16*10111 416*0 16*1105 464*0 4*10001 4*100a1 4*100c1 4*0 4*10061 4*100e1 8*0 4*10071 16*0 4*100b1
  //   8*0 4*10031 12*0 4*10041 4*10081 8*0 4*10021 12*0 4*10011 4*10091 8*0 16*13101 1392*0 2301 2301
  //   22301 22301 2301 2301 22301 22301 2301 2301 22301 22301 2301 2301 4*22301 2301 2301 22301 22301 2301
  //   2301 22301 22301 2301 2301 22301 22301 2301 2301 32*0 2301 22301 2301 22301 2301 22301 2301 22301
  //   2301 22301 2301 22301 2301 22301 2301 22301 16*0 2701 22701 2701 22701 2701 22701 2701 22701 2701
  //   22701 2701 22701 2701 22701 2701 22701 16*0 16*30100 240*0 16*34300
endmodule

module branchComp (
  input  [31:0] rs1,
  input  [31:0] rs2,
  input  BrUn,
  output BrLt,
  output BrEq
);

  wire BrEqSigned, BrEqUnsigned, BrLtSigned, BrLtUnsigned;

  Comparator #(.width(32)) comparator_1 (.a(rs1), .b(rs2), .eq(BrEqSigned), .lt(BrLtSigned));  // open: gt
  Comparator #(.width(32), .mode("unsigned")) comparator_2 (
    .a(rs1), .b(rs2), .eq(BrEqUnsigned), .lt(BrLtUnsigned));  // open: gt
  Multiplexer #(.enable("false")) multiplexer_1 (.in0(BrLtSigned), .in1(BrLtUnsigned), .out(BrLt), .sel(BrUn));
  Multiplexer #(.enable("false")) multiplexer_2 (.in0(BrEqSigned), .in1(BrEqUnsigned), .out(BrEq), .sel(BrUn));
endmodule
